// Logisim project processorSuprise.circ as structural Verilog: 6 circuits, main circuit main
module main (
  input  in_1,
  input  in_2,
  input  in_3,
  input  in_4
);

  wire alu_1_zero;
  wire [31:0] alu_1_y;

  Hex_Digit_Display hex_digit_display_1 (.value(alu_1_y[31:28]));  // open: dp
  ALU alu_1 (.F(3'b111), .B(32'h2), .A(32'h1), .Y(alu_1_y), .ZERO(alu_1_zero));
  LED led_1 (.in(alu_1_zero));
  Hex_Digit_Display hex_digit_display_2 (.value(alu_1_y[27:24]));  // open: dp
  Hex_Digit_Display hex_digit_display_3 (.value(alu_1_y[23:20]));  // open: dp
  Hex_Digit_Display hex_digit_display_4 (.value(alu_1_y[19:16]));  // open: dp
  Hex_Digit_Display hex_digit_display_5 (.value({in_4, in_3, in_2, in_1}));  // open: dp
  Hex_Digit_Display hex_digit_display_6 (.value(alu_1_y[15:12]));  // open: dp
  Hex_Digit_Display hex_digit_display_7 (.value(alu_1_y[11:8]));  // open: dp
  Hex_Digit_Display hex_digit_display_8 (.value(alu_1_y[7:4]));  // open: dp
  Hex_Digit_Display hex_digit_display_9 (.value(alu_1_y[3:0]));  // open: dp
endmodule

module ALU (
  input  [2:0] F,
  input  [31:0] B,
  input  [31:0] A,
  output [31:0] Y,
  output ZERO
);

  wire [31:0] adder_1_out, and_1_out, and_2_out, multiplexer_1_out, multiplexer_3_out, multiplier_1_out,
       not_1_out, or_1_out, shifter_1_out;

  assign not_1_out = ~B;  // NOT_Gate not_1, 32 bits wide
  Multiplexer #(.width(32), .enable("false")) multiplexer_1 (
    .in0(B), .in1(not_1_out), .out(multiplexer_1_out), .sel(F[2]));
  assign and_1_out = multiplexer_1_out & A;  // AND_Gate and_1, 32 bits wide
  assign or_1_out = multiplexer_1_out | A;  // OR_Gate or_1, 32 bits wide
  Adder #(.width(32)) adder_1 (.a(multiplexer_1_out), .b(A), .out(adder_1_out), .cin(F[2]));  // open: cout
  Multiplier #(.width(32)) multiplier_1 (.a(B), .b(A), .out(multiplier_1_out));  // open: cin, cout
  assign and_2_out = adder_1_out & 32'h80000000;  // AND_Gate and_2, 32 bits wide
  Shifter #(.width(32), .shift("lr")) shifter_1 (.in(and_2_out), .\dist ({5{1'b1}}), .out(shifter_1_out));
  Multiplexer #(.select(2), .width(32), .enable("false")) multiplexer_2 (
    .in0(and_1_out), .in1(or_1_out), .in2(adder_1_out), .in3(multiplexer_3_out), .out(Y), .sel(F[1:0]));
  Multiplexer #(.width(32), .enable("false")) multiplexer_3 (
    .in0(multiplier_1_out), .in1(shifter_1_out), .out(multiplexer_3_out), .sel(F[2]));
  Comparator #(.width(32), .mode("unsigned")) comparator_1 (.a(Y), .b({32{1'b0}}), .eq(ZERO));  // open: gt, lt
endmodule

module Datapath (
  output [31:0] dara_memory,
  output [7:0] v0,
  output [31:0] v0_2
);

  wire alu_1_zero, and_1_out, clock_1_out, controlunit_1_alusrc, controlunit_1_branch, controlunit_1_regdst,
       controlunit_1_regwrite;
  wire [2:0] bitselector_1_out, bitselector_2_out, bitselector_3_out, controlunit_1_alucontrol,
       multiplexer_2_out;
  wire [7:0] adder_1_out, adder_2_out, bitselector_5_out, register_1_q, shifter_1_out;
  wire [15:0] bitselector_4_out;
  wire [31:0] bit_extender_1_out, multiplexer_3_out, registerfile_1_rd1, registerfile_1_rd2, rom_1_data,
       shifter_2_out, shifter_3_out, shifter_4_out, shifter_5_out;

  Multiplexer #(.width(8), .enable("false")) multiplexer_1 (
    .in0(adder_1_out), .in1(adder_2_out), .out(v0), .sel(and_1_out));
  Clock clock_1 (.out(clock_1_out));
  Register register_1 (.D(v0), .Q(register_1_q), .clk(clock_1_out));  // open: en, clr
  Shifter #(.shift("lr")) shifter_1 (.in(register_1_q), .\dist (3'b010), .out(shifter_1_out));
  Adder adder_1 (.a(register_1_q), .b(8'h4), .out(adder_1_out));  // open: cin, cout
  ROM #(.dataWidth(32)) rom_1 (.addr(shifter_1_out), .data(rom_1_data));  // open: sel
  Shifter #(.width(32), .shift("lr")) shifter_2 (.in(rom_1_data), .\dist (5'b10101), .out(shifter_2_out));
  Shifter #(.width(32), .shift("lr")) shifter_3 (.in(rom_1_data), .\dist (5'b10000), .out(shifter_3_out));
  Shifter #(.width(32), .shift("lr")) shifter_4 (.in(rom_1_data), .\dist (5'b01011), .out(shifter_4_out));
  ControlUnit controlunit_1 (
    .Instruction(rom_1_data), .RegDst(controlunit_1_regdst), .RegWrite(controlunit_1_regwrite),
    .ALUControl(controlunit_1_alucontrol), .Branch(controlunit_1_branch), .ALUSrc(controlunit_1_alusrc));
  BitSelector #(.width(32), .group(3)) bitselector_1 (.in(shifter_2_out), .out(bitselector_1_out), .sel(4'b0000));
  BitSelector #(.width(32), .group(3)) bitselector_2 (.in(shifter_3_out), .out(bitselector_2_out), .sel(4'b0000));
  BitSelector #(.width(32), .group(3)) bitselector_3 (.in(shifter_4_out), .out(bitselector_3_out), .sel(4'b0000));
  BitSelector #(.width(32), .group(16)) bitselector_4 (.in(rom_1_data), .out(bitselector_4_out), .sel(1'b0));
  assign bit_extender_1_out = {{16{bitselector_4_out[15]}}, bitselector_4_out};  // Bit_Extender bit_extender_1
  RegisterFile registerfile_1 (
    .CLK(clock_1_out), .A1(bitselector_1_out), .WD3(dara_memory), .A2(bitselector_2_out),
    .WE3(controlunit_1_regwrite), .RD1(registerfile_1_rd1), .RD2(registerfile_1_rd2), .A3(multiplexer_2_out),
    .V0(v0_2));
  Multiplexer #(.width(3), .enable("false")) multiplexer_2 (
    .in0(bitselector_2_out), .in1(bitselector_3_out), .out(multiplexer_2_out), .sel(controlunit_1_regdst));
  Multiplexer #(.width(32), .enable("false")) multiplexer_3 (
    .in0(registerfile_1_rd2), .in1(bit_extender_1_out), .out(multiplexer_3_out), .sel(controlunit_1_alusrc));
  Shifter #(.width(32)) shifter_5 (.in(bit_extender_1_out), .\dist (5'b00010), .out(shifter_5_out));
  ALU alu_1 (
    .F(controlunit_1_alucontrol), .B(multiplexer_3_out), .A(registerfile_1_rd1), .Y(dara_memory),
    .ZERO(alu_1_zero));
  BitSelector #(.width(32), .group(8)) bitselector_5 (.in(shifter_5_out), .out(bitselector_5_out), .sel(2'b00));
  and and_1 (and_1_out, controlunit_1_branch, alu_1_zero);
  Adder adder_2 (.a(bitselector_5_out), .b(adder_1_out), .out(adder_2_out));  // open: cin, cout

  // Notes on the sheet:
  //   contents of rom_1 (hex, n*v repeats v):
  //   20040003 10800007 801020 802820 20a5ffff 20010001 10250003 70451002 1000fffb 20020001 1000ffff
endmodule

module Tests (
  output [31:0] Y,
  output [7:0] out_2,
  output [7:0] out_3,
  output [2:0] out_4
);

  BitSelector #(.width(32), .group(8)) bitselector_1 (.in(32'h12356789), .out(out_2), .sel(2'b01));
  BitSelector #(.width(32), .group(8)) bitselector_2 (.in(32'h12356789), .out(out_3), .sel(2'b01));
  BitSelector #(.group(3)) bitselector_3 (.in(out_3), .out(out_4), .sel(2'b00));

  assign Y = 32'hf4010207;

  // Notes on the sheet:
  //   binary values in Logisim. Convince yourself how the bits are displayed.
  //   Example 2: The bit selector is configured to have 32  
  //   bit group #1 (starting at index 0) is selected for the output.
  //   That is, the 8 bits 0x67 at bit indices 15..8  are sent to the output.
  //   Example 3: Now, assume that you want to extract 3 bits at   
  //   Example 1: A simple example that illustrates how 32-bit values are displayed as 
  //   input bits and 8 output bits. The parameter constant is 1, which means that   
  //   bit indices 10..8. This can be accoplished by putting two bit selecotrs in series.
endmodule

module RegisterFile (
  input  CLK,
  input  [2:0] A1,
  input  [31:0] WD3,
  input  [2:0] A2,
  input  WE3,
  input  [2:0] A3,
  output [31:0] RD1,
  output [31:0] RD2,
  output [31:0] V0
);

  wire and_1_out, and_2_out, and_3_out, and_4_out, and_5_out, and_6_out, and_7_out, and_8_out,
       decoder_1_out0, decoder_1_out1, decoder_1_out2, decoder_1_out3, decoder_1_out4, decoder_1_out5,
       decoder_1_out6, decoder_1_out7;
  wire [31:0] _0_q, register_1_q, register_3_q, register_4_q, register_5_q, register_6_q, register_7_q;

  Decoder #(.select(3)) decoder_1 (
    .out0(decoder_1_out0), .out1(decoder_1_out1), .out2(decoder_1_out2), .out3(decoder_1_out3),
    .out4(decoder_1_out4), .out5(decoder_1_out5), .out6(decoder_1_out6), .out7(decoder_1_out7), .sel(A3));  // open: en
  and and_1 (and_1_out, WE3, decoder_1_out0);
  and and_2 (and_2_out, WE3, decoder_1_out1);
  and and_3 (and_3_out, WE3, decoder_1_out2);
  and and_4 (and_4_out, WE3, decoder_1_out3);
  and and_5 (and_5_out, WE3, decoder_1_out4);
  and and_6 (and_6_out, WE3, decoder_1_out5);
  and and_7 (and_7_out, WE3, decoder_1_out6);
  and and_8 (and_8_out, WE3, decoder_1_out7);
  Register #(.width(32)) _0 (.D({32{1'b0}}), .en(and_1_out), .Q(_0_q), .clk(CLK));  // open: clr
  Register #(.width(32)) register_1 (.D(WD3), .en(and_2_out), .Q(register_1_q), .clk(CLK));  // open: clr
  Register #(.width(32)) register_2 (.D(WD3), .en(and_3_out), .Q(V0), .clk(CLK));  // open: clr
  Register #(.width(32)) register_3 (.D(WD3), .en(and_4_out), .Q(register_3_q), .clk(CLK));  // open: clr
  Register #(.width(32)) register_4 (.D(WD3), .en(and_5_out), .Q(register_4_q), .clk(CLK));  // open: clr
  Register #(.width(32)) register_5 (.D(WD3), .en(and_6_out), .Q(register_5_q), .clk(CLK));  // open: clr
  Register #(.width(32)) register_6 (.D(WD3), .en(and_7_out), .Q(register_6_q), .clk(CLK));  // open: clr
  Register #(.width(32)) register_7 (.D(WD3), .en(and_8_out), .Q(register_7_q), .clk(CLK));  // open: clr
  Multiplexer #(.select(3), .width(32)) multiplexer_1 (
    .in0(_0_q), .in1(register_1_q), .in2(V0), .in3(register_3_q), .in4(register_4_q), .in5(register_5_q),
    .in6(register_6_q), .in7(register_7_q), .out(RD1), .sel(A1));  // open: en
  Multiplexer #(.select(3), .width(32)) multiplexer_2 (
    .in0(_0_q), .in1(register_1_q), .in2(V0), .in3(register_3_q), .in4(register_4_q), .in5(register_5_q),
    .in6(register_6_q), .in7(register_7_q), .out(RD2), .sel(A2));  // open: en
endmodule

module ControlUnit (
  input  [31:0] Instruction,
  output RegDst,
  output RegWrite,
  output ALUSrc,
  output [2:0] ALUControl,
  output Branch
);

  wire comparator_2_eq, comparator_3_eq;
  wire [2:0] multiplexer_1_out;
  wire [5:0] bitselector_1_out;
  wire [31:0] shifter_1_out;

  Shifter #(.width(32), .shift("lr")) shifter_1 (.in(Instruction), .\dist (5'b11010), .out(shifter_1_out));
  BitSelector #(.width(32), .group(6)) bitselector_1 (.in(shifter_1_out), .out(bitselector_1_out), .sel(3'b000));
  Comparator #(.width(6), .mode("unsigned")) comparator_1 (
    .a(bitselector_1_out), .b(6'b001000), .eq(ALUSrc));  // open: gt, lt
  Comparator #(.width(6), .mode("unsigned")) comparator_2 (
    .a(bitselector_1_out), .b({6{1'b0}}), .eq(comparator_2_eq));  // open: gt, lt
  Comparator #(.width(6), .mode("unsigned")) comparator_3 (
    .a(bitselector_1_out), .b(6'b011100), .eq(comparator_3_eq));  // open: gt, lt
  Comparator #(.width(6), .mode("unsigned")) comparator_4 (
    .a(bitselector_1_out), .b(6'b000100), .eq(Branch));  // open: gt, lt
  Multiplexer #(.width(3), .enable("false")) multiplexer_1 (
    .in0(3'b010), .in1(3'b110), .out(multiplexer_1_out), .sel(Branch));
  or or_1 (RegDst, ALUSrc, comparator_3_eq, comparator_2_eq);
  or or_2 (RegDst, comparator_3_eq, comparator_2_eq);
  Multiplexer #(.width(3), .enable("false")) multiplexer_2 (
    .in0(multiplexer_1_out), .in1(3'b011), .out(ALUControl), .sel(comparator_3_eq));

  assign RegWrite = RegDst;
endmodule
